# Fritzing sketch LED on Sketch (saved by Fritzing 0.9.3b)
circuit board: 8.46667cm x 5.64444cm
breadboards: 1

parts:
  R1 = Resistor [tolerance=±5% resistance=220 package=THT]
  R2 = Resistor [tolerance=±5% resistance=220 package=THT]
  Part1 = Arduino Uno (Rev3)
  LED1 = LED - 5mm [color="Red (633nm)" package="5 mm [THT]"]
  LED2 = LED - 5mm [color="Red (633nm)" package="5 mm [THT]"]
  Part2 = SparkFun ESP8266 Thing
  HC-SR04_Sensor_1 = HC-SR04 Ultrasonic Distance Sensor
  R4 = Resistor [tolerance=±5% resistance=220 package="0402 [SMD]"]
  R5 = Resistor [tolerance=±5% resistance=220 package="0402 [SMD]"]

nets:
  N1: R1.Pin_0, LED2.anode
  N2: R1.Pin_1, Part1.D12/MISO
  N3: R2.Pin_0, LED1.anode
  N4: R2.Pin_1, Part2.GPIO5
  N5: Part1.D8, HC-SR04_Sensor_1.TRIG
  N6: Part1.D2, R4.Pin_0
  N7: Part1.D3_PWM, R5.Pin_0
  N8: Part1.D7, HC-SR04_Sensor_1.ECHO
  5V: Part1.5V, Part2.VIN, HC-SR04_Sensor_1.VCC
  GND: Part1.GND, LED1.cathode, LED2.cathode, Part2.GND, HC-SR04_Sensor_1.GND
  N9: Part2.GPIO13, R5.Pin_1
  N10: Part2.GPIO12, R4.Pin_1

notes:
  UNO LED
  D12
  NodeMCU LED
  D6
  Distance sensor
  7 = echo
  8=trig
  UNO NodeMCU
  D3(RX) ----> D3(TX)
  D2(TX) ----> D2(RX)
  And 2k ohm resistor between them!!
  Not to burn NodeMCU
  Sorry i cant find NodeMCU on fritzing so some OUTPUT may
  different.
